# Fritzing sketch paeiot-sensor-one (saved by Fritzing 0.9.3b)
circuit board: 1.7911cm x 3.68471cm
breadboards: 1

parts:
  AM2 = AM2302 Humidity and Temperature Sensor
  R1 = Resistor [tolerance=±5% resistance=220 package=THT]
  LED1 = LED - 3mm [color="Green (570nm)" package="3 mm [THT]"]
  J1 = male pin header, 3 pins [form="♂ (male)"]
  J2 = male pin header, 3 pins [form="♂ (male)"]
  J5 = female pin header, 3 pins [form="♀ (female)"]
  Part_1 = Arduino MKR WAN 1310
  AM1 = AM2302 Humidity and Temperature Sensor
  J4 = female pin header, 3 pins [form="♀ (female)"]

nets:
  N1: AM2.VDD, J4.pin2
  N2: AM2.DATA, J4.pin1
  N3: AM2.GND, J4.pin3
  N4: R1.Pin_0, LED1.anode
  N5: R1.Pin_1, Part_1.D0
  N6: LED1.cathode, J1.pin3, J2.pin3, Part_1.GND
  N7: J1.pin1, Part_1.D2
  N8: J1.pin2, J2.pin2, Part_1.+3V3
  N9: J2.pin1, Part_1.D3~
  N10: J5.pin1, AM1.DATA
  N11: J5.pin2, AM1.VDD
  N12: J5.pin3, AM1.GND
  N13: Part_1.RESET, Part_1.D14/TX
  N14: Part_1.D11/MOSI, Part_1.+5V

notes:
  paeiot
  sensor one
  v1.0 - 30 Aug 2021
  v1.0 30/08/2021

custom parts:
  Arduino MKR WAN 1310: The Arduino MKR WAN 1310 board provides a practical and cost effective solution to add LoRa® connectivity to projects requiring low power. This open source board can be connected to: the Arduino IoT Cloud, your own LoRa® network using the Arduino LoRa® PRO Gateway, existing LoRaWAN™ infrastructure like The Things Network, or even other boards using the direct connectivity mode.
